// Logisim project MipsOnBusCpu(已通关).circ as structural Verilog: 15 circuits, main circuit ◇指令译码器
module \单总线CPU_微程序  (
  output [21:0] \控制总线 
);

  wire and_1_out, CLK, comparator_1_eq, comparator_2_eq, equal, mips_alu_1_equal, not_1_out;
  wire [4:0] registerfile_1_p4, registerfile_1_p5, \微地址_状态 ;
  wire [11:0] Clks, \指令数 ;
  wire [31:0] AR_q, bit_extender_1_out, controlled_buffer_1_out, controlled_buffer_3_out, DR_q, IR,
       mips_alu_1_result, PC_q, ram_1_data, registerfile_1_p6, shifter_1_out, X_q, Z_q, \内部总线 ;

  // Probe on Clks
  Register #(.width(32), .trigger("rising"), .Select("low")) AR (
    .D(\内部总线 ), .en(\控制总线 [13]), .Q(AR_q), .clk(CLK));  // open: clr
  // Probe on controlled_buffer_3_out
  // Mips_Probe mips_probe_1: pin names not known; wires that end beside it: IR
  Register #(.width(32), .trigger("rising"), .Select("low")) X (
    .D(\内部总线 ), .en(\控制总线 [10]), .Q(X_q), .clk(CLK));  // open: clr
  // Probe on \指令数 
  RAM #(.addrWidth(10), .dataWidth(32), .bus("separate"), .Select("high")) ram_1 (
    .addr(AR_q[11:2]), .din(controlled_buffer_3_out), .data(ram_1_data), .str(\控制总线 [0]), .clk(CLK),
    .ld(\控制总线 [1]));  // open: sel, clr
  MIPS_ALU mips_alu_1 (
    .X(X_q), .Y(\内部总线 ), .Equal(mips_alu_1_equal), .Result(mips_alu_1_result), .ADD(\控制总线 [4]),
    .ADD4(\控制总线 [3]), .SLT(\控制总线 [2]));  // open: SUB
  assign controlled_buffer_1_out = \控制总线 [11] ? \内部总线  : 32'bz;  // Controlled_Buffer controlled_buffer_1
  assign controlled_buffer_1_out = \控制总线 [12] ? ram_1_data : 32'bz;  // Controlled_Buffer controlled_buffer_2
  assign controlled_buffer_3_out = \控制总线 [15] ? DR_q : 32'bz;  // Controlled_Buffer controlled_buffer_3
  // Probe on \内部总线 
  Register #(.width(32), .trigger("rising"), .Select("low")) PC (
    .D(\内部总线 ), .en(\控制总线 [14]), .Q(PC_q), .clk(CLK));  // open: clr
  Register #(.width(32), .trigger("rising"), .Select("low")) DR (
    .D(controlled_buffer_1_out), .Q(DR_q), .clk(CLK));  // open: en, clr
  Register #(.width(1), .trigger("rising"), .Select("low")) PSW (
    .D(mips_alu_1_equal), .en(\控制总线 [7]), .Q(equal), .clk(CLK));  // open: clr
  Register #(.width(32), .trigger("rising"), .Select("low")) Z (
    .D(mips_alu_1_result), .Q(Z_q), .clk(CLK));  // open: en, clr
  assign \内部总线  = \控制总线 [21] ? PC_q : 32'bz;  // Controlled_Buffer controlled_buffer_4
  assign \内部总线  = \控制总线 [20] ? DR_q : 32'bz;  // Controlled_Buffer controlled_buffer_5
  assign \内部总线  = \控制总线 [19] ? Z_q : 32'bz;  // Controlled_Buffer controlled_buffer_6
  assign \内部总线  = \控制总线 [17] ? bit_extender_1_out : 32'bz;  // Controlled_Buffer controlled_buffer_7
  assign \内部总线  = \控制总线 [16] ? shifter_1_out : 32'bz;  // Controlled_Buffer controlled_buffer_8
  Register #(.width(32), .trigger("rising"), .Select("low")) u_IR (
    .D(\内部总线 ), .en(\控制总线 [8]), .Q(IR), .clk(CLK));  // open: clr
  Comparator #(.width(32), .mode("twosComplement")) comparator_1 (
    .a(IR), .b(32'h1000ffff), .eq(comparator_1_eq));  // open: gt, lt
  Clock #(.highDuration(1), .lowDuration(1)) clock_1 (.out(CLK));
  \微程序控制器  \u_微程序控制器_1  (.CLK(CLK), .EQUAL(equal), .mAddr(\微地址_状态 ), .ControlBus(\控制总线 ), .\指令字 (IR));
  // Probe on \微地址_状态 
  // RegisterFile registerfile_1: pin names not known; wires that end beside it: \内部总线 , CLK, \控制总线 [9], registerfile_1_p4, registerfile_1_p5, registerfile_1_p6
  not not_1 (not_1_out, comparator_1_eq);
  Counter #(.width(12), .max('hfff), .ongoal("wrap"), .trigger("rising"), .behavior("new")) counter_1 (
    .count(not_1_out), .Q(Clks), .clk(CLK));  // open: load, D, carry, clr, preset, down
  assign bit_extender_1_out = {{16{IR[15]}}, IR[15:0]};  // Bit_Extender bit_extender_1
  assign \内部总线  = \控制总线 [18] ? registerfile_1_p6 : 32'bz;  // Controlled_Buffer controlled_buffer_9
  Multiplexer #(.select(1), .width(5), .disabled("Z"), .enable("false")) multiplexer_1 (
    .in0(IR[25:21]), .in1(IR[20:16]), .out(registerfile_1_p5), .sel(\控制总线 [6]));
  Multiplexer #(.select(1), .width(5), .disabled("Z"), .enable("false")) multiplexer_2 (
    .in0(IR[20:16]), .in1(IR[15:11]), .out(registerfile_1_p4), .sel(\控制总线 [5]));
  and and_1 (and_1_out, not_1_out, comparator_2_eq);
  Comparator #(.width(5), .mode("twosComplement")) comparator_2 (
    .a(5'b00011), .b(\微地址_状态 ), .eq(comparator_2_eq));  // open: gt, lt
  Shifter #(.width(32), .shift("ll")) shifter_1 (.in(bit_extender_1_out), .\dist (5'b00010), .out(shifter_1_out));
  Counter #(.width(12), .max('hfff), .ongoal("wrap"), .trigger("rising"), .behavior("old")) counter_2 (
    .count(and_1_out), .Q(\指令数 ), .clk(CLK));  // open: load, D, carry, clr, preset

  // Other names for the same wires on the sheet: rd[4:0] = IR[15:11]; rt[4:0] = IR[20:16]; rs[4:0] = IR[25:21];
  //   Write = \控制总线 [0]; READ = \控制总线 [1]; Slt = \控制总线 [2]; Add4 = \控制总线 [3]; Add = \控制总线 [4]; RegDst = \控制总线 [5];
  //   RegTgt = \控制总线 [6]; PSWin = \控制总线 [7]; IRin = \控制总线 [8]; Rin = \控制总线 [9]; Xin = \控制总线 [10]; DRin = \控制总线 [11];
  //   DREin = \控制总线 [12]; ARin = \控制总线 [13]; PCin = \控制总线 [14]; DREout = \控制总线 [15]; IR_A_out = \控制总线 [16];
  //   IR_I_out = \控制总线 [17]; Rout = \控制总线 [18]; Zout = \控制总线 [19]; DRout = \控制总线 [20]; PCout = \控制总线 [21]

  // Notes on the sheet:
  //   单总线结构 MIPS CPU
  //   主存
  //   外部总线
  //   内部总线
  //   微程序控制器
  //   Immediate32
  //   AddressOffset32
endmodule

// Decoder
module \指令译码器  (
  input  [31:0] IR,
  output LW,
  output SW,
  output BEQ,
  output ADDI,
  output SLT,
  output OtherInstr
);

  wire comparator_5_eq, comparator_6_eq;

  Comparator #(.width(6), .mode("twosComplement")) comparator_1 (
    .a(IR[31:26]), .b(6'b100011), .eq(LW));  // open: gt, lt
  Comparator #(.width(6), .mode("twosComplement")) comparator_2 (
    .a(IR[31:26]), .b(6'b101011), .eq(SW));  // open: gt, lt
  Comparator #(.width(6), .mode("twosComplement")) comparator_3 (
    .a(IR[31:26]), .b(6'b000100), .eq(BEQ));  // open: gt, lt
  Comparator #(.width(6), .mode("twosComplement")) comparator_4 (
    .a(IR[31:26]), .b(6'b001000), .eq(ADDI));  // open: gt, lt
  Comparator #(.width(6), .mode("twosComplement")) comparator_5 (
    .a(IR[31:26]), .b({6{1'b0}}), .eq(comparator_5_eq));  // open: gt, lt
  Comparator #(.width(6), .mode("twosComplement")) comparator_6 (
    .a(IR[5:0]), .b(6'b101010), .eq(comparator_6_eq));  // open: gt, lt
  and and_1 (SLT, comparator_5_eq, comparator_6_eq);
  nor nor_1 (OtherInstr, BEQ, SW, LW, ADDI, SLT);

  // Other names for the same wires on the sheet: FUNCT[5:0] = IR[5:0]; OP[5:0] = IR[31:26]

  // Notes on the sheet:
  //   常用常量
endmodule

// 控制器
module \微程序控制器  (
  input  EQUAL,
  input  [31:0] \指令字 ,
  input  CLK,
  output [4:0] mAddr,
  output [21:0] ControlBus
);

  wire ADDI, BEQ, LW, Other, P0, P1, P2, SLT, SW;
  wire [1:0] \条件判别测试逻辑_1_s0 ;
  wire [4:0] multiplexer_1_out, rom_1_data, \微程序入口查找逻辑_1_s0 ;

  \微程序入口查找逻辑  \u_微程序入口查找逻辑_1  (
    .LW(LW), .SW(SW), .BEQ(BEQ), .SLT(SLT), .ADDI(ADDI), .S4(\微程序入口查找逻辑_1_s0 [4]), .S3(\微程序入口查找逻辑_1_s0 [3]),
    .S2(\微程序入口查找逻辑_1_s0 [2]), .S1(\微程序入口查找逻辑_1_s0 [1]), .S0(\微程序入口查找逻辑_1_s0 [0]));
  // Probe on \微程序入口查找逻辑_1_s0 
  \条件判别测试逻辑  \u_条件判别测试逻辑_1  (.P0(P0), .P1(P1), .equal(EQUAL), .S1(\条件判别测试逻辑_1_s0 [1]), .S0(\条件判别测试逻辑_1_s0 [0]));
  Multiplexer #(.select(2), .width(5), .disabled("Z"), .enable("false")) multiplexer_1 (
    .in0(rom_1_data), .in1(\微程序入口查找逻辑_1_s0 ), .in2(5'b10000), .out(multiplexer_1_out), .sel(\条件判别测试逻辑_1_s0 ));  // open: in3
  // Probe on mAddr
  Register #(.width(5), .trigger("falling"), .Select("low")) register_1 (
    .D(multiplexer_1_out), .Q(mAddr), .clk(CLK));  // open: en, clr
  ROM #(.addrWidth(5), .dataWidth(30), .Select("high")) rom_1 (
    .addr(mAddr), .data({ControlBus, P0, P1, P2, rom_1_data}));
  \指令译码器  \u_指令译码器_1  (.IR(\指令字 ), .LW(LW), .SW(SW), .BEQ(BEQ), .ADDI(ADDI), .SLT(SLT), .OtherInstr(Other));

  // Notes on the sheet:
  //   不要改变此引脚区域内容，也不要改变封装形式
  //   微程序入口查找逻辑
  //   判别测试逻辑
  //   微程序入口
  //   beq分支
  //   下址字段
  //   输入输出引脚
  //   μAR
  //   时钟是上跳沿还是下跳沿有效？
  //   微地址
  //   微程序控制器（下址字段法）
  //   控制存储器
  //   contents of rom_1 (hex, n*v repeats v):
  //   20240001 802 8500203 10010080 4040005 2001006 8200007 100208 10020000 404000a 200100b 820000c
  //   408400d 800100 404000f 400c040 20040011 1001012 8400000 4040014 4004415 8022000 4040017 2001018
  //   8020000
  //   指令译码器
  //   微指令
  //   控制字段
  //   指令译码信号
  //   判断逻辑
  //   指令译码逻辑ID
endmodule

module \微程序入口查找逻辑  (
  input  LW,
  input  SW,
  input  BEQ,
  input  SLT,
  input  ADDI,
  output S4,
  output S3,
  output S2,
  output S1,
  output S0
);

  wire and_1_out, and_2_out, and_3_out, and_4_out, and_5_out, and_6_out, and_7_out, and_8_out, and_9_out,
       and_10_out, and_11_out, and_12_out, and_13_out, and_14_out, and_15_out, and_16_out, and_17_out,
       and_18_out, and_19_out, and_20_out, and_21_out, and_22_out, and_23_out, and_24_out, and_25_out,
       and_26_out, and_27_out, and_28_out, and_29_out, and_30_out, and_31_out, and_32_out, and_33_out,
       and_34_out, and_35_out, and_36_out, and_37_out, and_38_out, and_39_out, and_40_out, and_41_out,
       and_42_out, and_43_out, and_44_out, and_45_out, and_46_out, and_47_out, and_48_out, not_1_out,
       not_2_out, not_3_out, not_4_out, not_5_out, not_6_out, not_7_out, not_8_out, not_9_out, not_10_out,
       not_11_out, not_12_out, not_13_out, not_14_out, not_15_out, not_16_out, not_17_out, not_18_out,
       not_19_out, not_20_out, not_21_out, not_22_out, not_23_out, not_24_out, not_25_out, not_26_out,
       not_27_out, not_28_out, not_29_out, not_30_out, not_31_out, not_32_out, not_33_out, not_34_out,
       not_35_out, not_36_out, not_37_out, not_38_out, not_39_out, not_40_out, not_41_out, not_42_out,
       not_43_out, not_44_out, not_45_out, not_46_out, not_47_out, not_48_out, or_3_out, or_4_out;

  not not_1 (not_1_out, LW);
  not not_2 (not_2_out, SW);
  not not_3 (not_3_out, LW);
  not not_4 (not_4_out, SW);
  not not_5 (not_5_out, LW);
  not not_6 (not_6_out, LW);
  not not_7 (not_7_out, SW);
  not not_8 (not_8_out, SW);
  not not_9 (not_9_out, LW);
  not not_10 (not_10_out, SW);
  not not_11 (not_11_out, LW);
  not not_12 (not_12_out, SW);
  not not_13 (not_13_out, LW);
  not not_14 (not_14_out, SW);
  not not_15 (not_15_out, LW);
  not not_16 (not_16_out, LW);
  not not_17 (not_17_out, SW);
  and and_1 (and_1_out, not_1_out, not_2_out);
  not not_18 (not_18_out, BEQ);
  not not_19 (not_19_out, ADDI);
  and and_2 (and_2_out, not_3_out, not_4_out);
  not not_20 (not_20_out, BEQ);
  not not_21 (not_21_out, SLT);
  and and_3 (and_3_out, not_5_out, SW);
  not not_22 (not_22_out, BEQ);
  not not_23 (not_23_out, SLT);
  not not_24 (not_24_out, ADDI);
  and and_4 (and_4_out, not_6_out, not_7_out);
  not not_25 (not_25_out, SLT);
  not not_26 (not_26_out, ADDI);
  and and_5 (and_5_out, LW, not_8_out);
  not not_27 (not_27_out, BEQ);
  not not_28 (not_28_out, SLT);
  not not_29 (not_29_out, ADDI);
  and and_6 (and_6_out, not_9_out, not_10_out);
  not not_30 (not_30_out, SLT);
  not not_31 (not_31_out, ADDI);
  not not_32 (not_32_out, LW);
  not not_33 (not_33_out, SW);
  and and_7 (and_7_out, not_11_out, not_12_out);
  not not_34 (not_34_out, SLT);
  not not_35 (not_35_out, ADDI);
  and and_8 (and_8_out, not_13_out, not_14_out);
  not not_36 (not_36_out, BEQ);
  not not_37 (not_37_out, ADDI);
  not not_38 (not_38_out, LW);
  not not_39 (not_39_out, SW);
  and and_9 (and_9_out, not_15_out, SW);
  not not_40 (not_40_out, BEQ);
  not not_41 (not_41_out, SLT);
  not not_42 (not_42_out, ADDI);
  and and_10 (and_10_out, not_16_out, not_17_out);
  not not_43 (not_43_out, BEQ);
  not not_44 (not_44_out, ADDI);
  and and_11 (and_11_out, and_1_out, not_18_out);
  and and_12 (and_12_out, and_11_out, and_13_out);
  and and_13 (and_13_out, SLT, not_19_out);
  and and_14 (and_14_out, and_2_out, not_20_out);
  and and_15 (and_15_out, and_14_out, and_16_out);
  and and_16 (and_16_out, not_21_out, ADDI);
  and and_17 (and_17_out, and_3_out, not_22_out);
  and and_18 (and_18_out, and_17_out, and_19_out);
  and and_19 (and_19_out, not_23_out, not_24_out);
  and and_20 (and_20_out, and_4_out, BEQ);
  and and_21 (and_21_out, and_20_out, and_22_out);
  and and_22 (and_22_out, not_25_out, not_26_out);
  and and_23 (and_23_out, and_5_out, not_27_out);
  and and_24 (and_24_out, and_23_out, and_25_out);
  and and_25 (and_25_out, not_28_out, not_29_out);
  and and_26 (and_26_out, and_6_out, BEQ);
  and and_27 (and_27_out, and_26_out, and_28_out);
  and and_28 (and_28_out, not_30_out, not_31_out);
  and and_29 (and_29_out, not_32_out, not_33_out);
  and and_30 (and_30_out, and_29_out, not_45_out);
  not not_45 (not_45_out, BEQ);
  not not_46 (not_46_out, SLT);
  and and_31 (and_31_out, not_46_out, ADDI);
  and and_32 (and_32_out, and_7_out, BEQ);
  and and_33 (and_33_out, and_32_out, and_34_out);
  and and_34 (and_34_out, not_34_out, not_35_out);
  and and_35 (and_35_out, and_8_out, not_36_out);
  and and_36 (and_36_out, and_35_out, and_37_out);
  and and_37 (and_37_out, SLT, not_37_out);
  and and_38 (and_38_out, not_38_out, not_39_out);
  and and_39 (and_39_out, and_38_out, not_47_out);
  not not_47 (not_47_out, BEQ);
  not not_48 (not_48_out, SLT);
  and and_40 (and_40_out, not_48_out, ADDI);
  and and_41 (and_41_out, and_9_out, not_40_out);
  and and_42 (and_42_out, and_41_out, and_43_out);
  and and_43 (and_43_out, not_41_out, not_42_out);
  and and_44 (and_44_out, and_10_out, not_43_out);
  and and_45 (and_45_out, and_44_out, and_46_out);
  and and_46 (and_46_out, SLT, not_44_out);
  or or_1 (S4, and_12_out, and_15_out);
  or or_2 (S3, and_18_out, and_21_out);
  or or_3 (or_3_out, and_24_out, and_27_out);
  and and_47 (and_47_out, and_30_out, and_31_out);
  or or_4 (or_4_out, and_33_out, and_36_out);
  and and_48 (and_48_out, and_39_out, and_40_out);
  or or_5 (S0, and_42_out, and_45_out);
  or or_6 (S2, or_3_out, and_47_out);
  or or_7 (S1, or_4_out, and_48_out);
endmodule

module \条件判别测试逻辑  (
  input  P0,
  input  P1,
  input  equal,
  output S1,
  output S0
);

  wire and_1_out, and_2_out, and_3_out, and_5_out, and_6_out, not_1_out, not_2_out, not_3_out, not_4_out;

  not not_1 (not_1_out, P0);
  not not_2 (not_2_out, P1);
  not not_3 (not_3_out, P1);
  and and_1 (and_1_out, not_1_out, P1);
  and and_2 (and_2_out, P0, not_2_out);
  not not_4 (not_4_out, equal);
  and and_3 (and_3_out, P0, not_3_out);
  and and_4 (S1, and_1_out, equal);
  and and_5 (and_5_out, and_2_out, not_4_out);
  and and_6 (and_6_out, and_3_out, equal);
  or or_1 (S0, and_5_out, and_6_out);
endmodule

// 硬布线
module \硬布线控制器  (
  input  EQUAL,
  input  [31:0] \指令字 ,
  input  CLK,
  output [4:0] statu,
  output [21:0] ControlBus
);

  wire ADDI, BEQ, LW, Other, SLT, SW;
  wire [4:0] \硬布线状态机_1_n0 ;
  wire [7:0] rom_1_data;

  \硬布线状态机  \u_硬布线状态机_1  (
    .S4(statu[4]), .S3(statu[3]), .S2(statu[2]), .S1(statu[1]), .S0(statu[0]), .LW(LW), .SW(SW), .BEQ(BEQ),
    .SLT(SLT), .ADDI(ADDI), .EQUAL(EQUAL), .N4(\硬布线状态机_1_n0 [4]), .N3(\硬布线状态机_1_n0 [3]),
    .N2(\硬布线状态机_1_n0 [2]), .N1(\硬布线状态机_1_n0 [1]), .N0(\硬布线状态机_1_n0 [0]));
  // Probe on \硬布线状态机_1_n0 
  Register #(.width(5), .trigger("falling"), .Select("low")) register_1 (
    .D(\硬布线状态机_1_n0 ), .en(1'b1), .Q(statu), .clk(CLK));  // open: clr
  \指令译码器  \u_指令译码器_1  (.IR(\指令字 ), .LW(LW), .SW(SW), .BEQ(BEQ), .ADDI(ADDI), .SLT(SLT), .OtherInstr(Other));
  ROM #(.addrWidth(5), .dataWidth(30), .Select("high")) rom_1 (.addr(statu), .data({ControlBus, rom_1_data}));

  // Other names for the same wires on the sheet: Write = ControlBus[0]; READ = ControlBus[1]; Slt_t = ControlBus[2];
  //   Add4 = ControlBus[3]; Add = ControlBus[4]; RegDst = ControlBus[5]; RegTgt = ControlBus[6];
  //   PSWin = ControlBus[7]; IRin = ControlBus[8]; Rin = ControlBus[9]; Xin = ControlBus[10]; DRin = ControlBus[11];
  //   DREin = ControlBus[12]; ARin = ControlBus[13]; PCin = ControlBus[14]; DREout = ControlBus[15];
  //   IR_A_out = ControlBus[16]; IR_I_out = ControlBus[17]; Rout = ControlBus[18]; Zout = ControlBus[19];
  //   DRout = ControlBus[20]; PCout = ControlBus[21]

  // Notes on the sheet:
  //   不要改变此引脚区域内容，也不要改变封装形式
  //   输入输出引脚
  //   时钟是上跳沿还是下跳沿有效？
  //   状态寄存器
  //   指令译码器
  //   控制存储器
  //   contents of rom_1 (hex, n*v repeats v):
  //   20240001 802 8500203 10010080 4040005 2001006 8200007 100208 10020000 404000a 200100b 820000c
  //   408400d 800100 404000f 400c040 20040011 1001012 8400000 4040014 4004415 8022000 4040017 2001018
  //   8020000
  //   指令译码信号
  //   控制字段
  //   微指令
  //   指令译码逻辑ID
endmodule

module \硬布线状态机  (
  input  S4,
  input  S3,
  input  S2,
  input  S1,
  input  S0,
  input  LW,
  input  SW,
  input  BEQ,
  input  SLT,
  input  ADDI,
  input  EQUAL,
  output N4,
  output N3,
  output N2,
  output N1,
  output N0
);

  wire and_1_out, and_2_out, and_3_out, and_4_out, and_5_out, and_6_out, and_7_out, and_8_out, and_9_out,
       and_10_out, and_11_out, and_12_out, and_13_out, and_14_out, and_15_out, and_16_out, and_17_out,
       and_18_out, and_19_out, and_20_out, and_21_out, and_22_out, and_23_out, and_24_out, and_25_out,
       and_26_out, and_27_out, and_28_out, and_29_out, and_30_out, and_31_out, and_32_out, and_33_out,
       and_34_out, and_35_out, and_36_out, and_37_out, and_38_out, and_39_out, and_40_out, and_41_out,
       and_42_out, and_43_out, and_44_out, and_45_out, and_46_out, and_47_out, and_48_out, and_49_out,
       and_50_out, and_51_out, and_52_out, and_53_out, and_54_out, and_55_out, and_56_out, and_57_out,
       and_58_out, and_59_out, and_60_out, and_61_out, and_62_out, and_63_out, and_64_out, and_65_out,
       and_66_out, and_67_out, and_68_out, and_69_out, and_70_out, and_71_out, and_72_out, and_73_out,
       and_74_out, and_75_out, and_76_out, and_77_out, and_78_out, and_79_out, and_80_out, and_81_out,
       and_82_out, and_83_out, and_84_out, and_85_out, and_86_out, and_87_out, and_88_out, and_89_out,
       and_90_out, and_91_out, and_92_out, and_93_out, and_94_out, and_95_out, and_96_out, and_97_out,
       and_98_out, and_99_out, and_100_out, and_101_out, and_102_out, and_103_out, and_104_out, and_105_out,
       and_106_out, and_107_out, and_108_out, and_109_out, and_110_out, and_111_out, and_112_out,
       and_113_out, and_114_out, and_115_out, and_116_out, and_117_out, and_118_out, and_119_out,
       and_120_out, and_121_out, and_122_out, and_123_out, and_124_out, and_125_out, and_126_out,
       and_127_out, and_128_out, and_129_out, and_130_out, and_131_out, and_132_out, and_133_out,
       and_134_out, and_135_out, and_136_out, and_137_out, and_138_out, and_139_out, and_140_out,
       and_141_out, and_142_out, and_143_out, and_144_out, and_145_out, and_146_out, and_147_out,
       and_148_out, and_149_out, and_150_out, and_151_out, and_152_out, and_153_out, and_154_out,
       and_155_out, and_156_out, and_157_out, and_158_out, and_159_out, and_160_out, and_161_out,
       and_162_out, and_163_out, and_164_out, and_165_out, and_166_out, and_167_out, and_168_out,
       and_169_out, and_170_out, and_171_out, and_172_out, and_173_out, and_174_out, and_175_out,
       and_176_out, and_177_out, and_178_out, and_179_out, and_180_out, and_181_out, and_182_out,
       and_183_out, and_184_out, and_185_out, and_186_out, and_187_out, and_188_out, and_189_out,
       and_190_out, and_191_out, and_192_out, and_193_out, and_194_out, and_195_out, and_196_out,
       and_197_out, and_198_out, and_199_out, and_200_out, and_201_out, and_202_out, and_203_out,
       and_204_out, and_205_out, and_206_out, and_207_out, and_208_out, and_209_out, and_210_out,
       and_211_out, and_212_out, and_213_out, and_214_out, and_215_out, and_216_out, and_217_out,
       and_218_out, and_219_out, and_220_out, and_221_out, and_222_out, and_223_out, and_224_out,
       and_225_out, and_226_out, and_227_out, and_228_out, and_229_out, not_1_out, not_2_out, not_3_out,
       not_4_out, not_5_out, not_6_out, not_7_out, not_8_out, not_9_out, not_10_out, not_11_out, not_12_out,
       not_13_out, not_14_out, not_15_out, not_16_out, not_17_out, not_18_out, not_19_out, not_20_out,
       not_21_out, not_22_out, not_23_out, not_24_out, not_25_out, not_26_out, not_27_out, not_28_out,
       not_29_out, not_30_out, not_31_out, not_32_out, not_33_out, not_34_out, not_35_out, not_36_out,
       not_37_out, not_38_out, not_39_out, not_40_out, not_41_out, not_42_out, not_43_out, not_44_out,
       not_45_out, not_46_out, not_47_out, not_48_out, not_49_out, not_50_out, not_51_out, not_52_out,
       not_53_out, not_54_out, not_55_out, not_56_out, not_57_out, not_58_out, not_59_out, not_60_out,
       not_61_out, not_62_out, not_63_out, not_64_out, not_65_out, not_66_out, not_67_out, not_68_out,
       not_69_out, not_70_out, not_71_out, not_72_out, not_73_out, not_74_out, not_75_out, not_76_out,
       not_77_out, not_78_out, not_79_out, not_80_out, not_81_out, not_82_out, not_83_out, not_84_out,
       not_85_out, not_86_out, not_87_out, not_88_out, not_89_out, not_90_out, not_91_out, not_92_out,
       not_93_out, not_94_out, not_95_out, not_96_out, not_97_out, not_98_out, not_99_out, not_100_out,
       not_101_out, not_102_out, not_103_out, not_104_out, not_105_out, not_106_out, not_107_out,
       not_108_out, not_109_out, not_110_out, not_111_out, not_112_out, not_113_out, not_114_out,
       not_115_out, not_116_out, not_117_out, not_118_out, not_119_out, not_120_out, not_121_out,
       not_122_out, not_123_out, not_124_out, not_125_out, not_126_out, not_127_out, not_128_out,
       not_129_out, not_130_out, not_131_out, not_132_out, not_133_out, not_134_out, not_135_out,
       not_136_out, not_137_out, not_138_out, not_139_out, not_140_out, not_141_out, not_142_out,
       not_143_out, not_144_out, not_145_out, not_146_out, not_147_out, not_148_out, not_149_out,
       not_150_out, not_151_out, not_152_out, or_1_out, or_2_out, or_3_out, or_4_out, or_5_out, or_6_out,
       or_7_out, or_8_out, or_9_out, or_10_out, or_11_out, or_12_out, or_13_out, or_14_out, or_15_out,
       or_16_out, or_17_out, or_18_out, or_19_out, or_20_out, or_21_out, or_22_out, or_23_out, or_24_out,
       or_25_out, or_26_out, or_27_out, or_28_out, or_29_out, or_30_out, or_31_out, or_32_out, or_33_out,
       or_34_out, or_35_out, or_37_out, or_38_out, or_40_out, or_41_out, or_43_out, or_44_out, or_46_out,
       or_47_out, or_49_out;

  not not_1 (not_1_out, S4);
  not not_2 (not_2_out, S3);
  not not_3 (not_3_out, S4);
  not not_4 (not_4_out, S3);
  not not_5 (not_5_out, S4);
  not not_6 (not_6_out, S3);
  not not_7 (not_7_out, S4);
  not not_8 (not_8_out, S3);
  not not_9 (not_9_out, S4);
  not not_10 (not_10_out, S3);
  not not_11 (not_11_out, S4);
  not not_12 (not_12_out, S3);
  not not_13 (not_13_out, S4);
  not not_14 (not_14_out, S3);
  not not_15 (not_15_out, S4);
  not not_16 (not_16_out, S3);
  not not_17 (not_17_out, S4);
  not not_18 (not_18_out, S4);
  not not_19 (not_19_out, S3);
  not not_20 (not_20_out, S3);
  not not_21 (not_21_out, S4);
  not not_22 (not_22_out, S3);
  not not_23 (not_23_out, S4);
  not not_24 (not_24_out, S3);
  not not_25 (not_25_out, S4);
  not not_26 (not_26_out, S3);
  not not_27 (not_27_out, S4);
  not not_28 (not_28_out, S3);
  not not_29 (not_29_out, S4);
  not not_30 (not_30_out, S3);
  not not_31 (not_31_out, S4);
  not not_32 (not_32_out, S4);
  not not_33 (not_33_out, S3);
  not not_34 (not_34_out, S4);
  not not_35 (not_35_out, S3);
  not not_36 (not_36_out, S4);
  not not_37 (not_37_out, S3);
  not not_38 (not_38_out, S4);
  not not_39 (not_39_out, S3);
  not not_40 (not_40_out, S4);
  not not_41 (not_41_out, S3);
  not not_42 (not_42_out, S4);
  not not_43 (not_43_out, S4);
  not not_44 (not_44_out, S3);
  not not_45 (not_45_out, S3);
  and and_1 (and_1_out, not_1_out, not_2_out);
  not not_46 (not_46_out, S2);
  and and_2 (and_2_out, S1, S0);
  and and_3 (and_3_out, not_3_out, not_4_out);
  not not_47 (not_47_out, S2);
  and and_4 (and_4_out, S1, S0);
  not not_48 (not_48_out, S4);
  not not_49 (not_49_out, S3);
  not not_50 (not_50_out, S3);
  not not_51 (not_51_out, S3);
  not not_52 (not_52_out, S3);
  not not_53 (not_53_out, S3);
  not not_54 (not_54_out, S3);
  and and_5 (and_5_out, not_5_out, not_6_out);
  not not_55 (not_55_out, S2);
  and and_6 (and_6_out, S1, S0);
  and and_7 (and_7_out, not_7_out, not_8_out);
  not not_56 (not_56_out, S2);
  and and_8 (and_8_out, S1, S0);
  not not_57 (not_57_out, S4);
  not not_58 (not_58_out, S3);
  not not_59 (not_59_out, S4);
  not not_60 (not_60_out, S4);
  not not_61 (not_61_out, S4);
  not not_62 (not_62_out, S4);
  not not_63 (not_63_out, S4);
  not not_64 (not_64_out, S3);
  and and_9 (and_9_out, not_9_out, not_10_out);
  not not_65 (not_65_out, S2);
  and and_10 (and_10_out, S1, S0);
  and and_11 (and_11_out, not_11_out, not_12_out);
  not not_66 (not_66_out, S2);
  and and_12 (and_12_out, S1, S0);
  not not_67 (not_67_out, S4);
  not not_68 (not_68_out, S3);
  and and_13 (and_13_out, not_13_out, not_14_out);
  not not_69 (not_69_out, S1);
  not not_70 (not_70_out, S0);
  and and_14 (and_14_out, not_15_out, not_16_out);
  not not_71 (not_71_out, S1);
  not not_72 (not_72_out, S4);
  not not_73 (not_73_out, S3);
  and and_15 (and_15_out, not_17_out, S3);
  not not_74 (not_74_out, S2);
  and and_16 (and_16_out, not_18_out, S3);
  not not_75 (not_75_out, S1);
  not not_76 (not_76_out, S0);
  not not_77 (not_77_out, S4);
  and and_17 (and_17_out, S4, not_19_out);
  not not_78 (not_78_out, S2);
  and and_18 (and_18_out, S4, not_20_out);
  not not_79 (not_79_out, S1);
  not not_80 (not_80_out, S0);
  not not_81 (not_81_out, S3);
  and and_19 (and_19_out, not_21_out, not_22_out);
  not not_82 (not_82_out, S2);
  not not_83 (not_83_out, S1);
  and and_20 (and_20_out, not_23_out, not_24_out);
  not not_84 (not_84_out, S2);
  not not_85 (not_85_out, S0);
  not not_86 (not_86_out, S4);
  not not_87 (not_87_out, S3);
  and and_21 (and_21_out, not_25_out, not_26_out);
  not not_88 (not_88_out, S2);
  and and_22 (and_22_out, S1, S0);
  and and_23 (and_23_out, not_27_out, not_28_out);
  not not_89 (not_89_out, S2);
  and and_24 (and_24_out, S1, S0);
  not not_90 (not_90_out, S4);
  not not_91 (not_91_out, S3);
  and and_25 (and_25_out, not_29_out, not_30_out);
  not not_92 (not_92_out, S0);
  and and_26 (and_26_out, not_31_out, S3);
  not not_93 (not_93_out, S2);
  not not_94 (not_94_out, S1);
  not not_95 (not_95_out, S4);
  and and_27 (and_27_out, not_32_out, S3);
  not not_96 (not_96_out, S0);
  and and_28 (and_28_out, S4, not_33_out);
  not not_97 (not_97_out, S2);
  not not_98 (not_98_out, S1);
  not not_99 (not_99_out, S3);
  and and_29 (and_29_out, not_34_out, not_35_out);
  not not_100 (not_100_out, S2);
  not not_101 (not_101_out, S1);
  not not_102 (not_102_out, S0);
  and and_30 (and_30_out, not_36_out, not_37_out);
  not not_103 (not_103_out, S2);
  not not_104 (not_104_out, S0);
  not not_105 (not_105_out, S4);
  not not_106 (not_106_out, S3);
  and and_31 (and_31_out, not_38_out, not_39_out);
  not not_107 (not_107_out, S2);
  and and_32 (and_32_out, S1, S0);
  and and_33 (and_33_out, not_40_out, not_41_out);
  not not_108 (not_108_out, S1);
  not not_109 (not_109_out, S0);
  not not_110 (not_110_out, S4);
  not not_111 (not_111_out, S3);
  and and_34 (and_34_out, not_42_out, S3);
  not not_112 (not_112_out, S2);
  not not_113 (not_113_out, S0);
  and and_35 (and_35_out, not_43_out, S3);
  not not_114 (not_114_out, S1);
  not not_115 (not_115_out, S0);
  not not_116 (not_116_out, S4);
  and and_36 (and_36_out, S4, not_44_out);
  not not_117 (not_117_out, S2);
  not not_118 (not_118_out, S1);
  not not_119 (not_119_out, S0);
  and and_37 (and_37_out, S4, not_45_out);
  not not_120 (not_120_out, S1);
  not not_121 (not_121_out, S0);
  not not_122 (not_122_out, S3);
  and and_38 (and_38_out, and_1_out, not_46_out);
  and and_39 (and_39_out, and_2_out, SLT);
  and and_40 (and_40_out, and_3_out, not_47_out);
  and and_41 (and_41_out, and_4_out, ADDI);
  and and_42 (and_42_out, not_48_out, S3);
  and and_43 (and_43_out, S1, S0);
  and and_44 (and_44_out, S4, not_49_out);
  not not_123 (not_123_out, S2);
  not not_124 (not_124_out, S1);
  not not_125 (not_125_out, S0);
  and and_45 (and_45_out, S4, not_50_out);
  not not_126 (not_126_out, S2);
  not not_127 (not_127_out, S1);
  and and_46 (and_46_out, S4, not_51_out);
  not not_128 (not_128_out, S2);
  and and_47 (and_47_out, S4, not_52_out);
  not not_129 (not_129_out, S1);
  not not_130 (not_130_out, S0);
  and and_48 (and_48_out, S4, not_53_out);
  not not_131 (not_131_out, S0);
  and and_49 (and_49_out, S4, not_54_out);
  and and_50 (and_50_out, and_5_out, not_55_out);
  and and_51 (and_51_out, and_6_out, SW);
  and and_52 (and_52_out, and_7_out, not_56_out);
  and and_53 (and_53_out, and_8_out, BEQ);
  and and_54 (and_54_out, not_57_out, not_58_out);
  and and_55 (and_55_out, not_59_out, S3);
  not not_132 (not_132_out, S2);
  not not_133 (not_133_out, S1);
  and and_56 (and_56_out, not_60_out, S3);
  not not_134 (not_134_out, S2);
  not not_135 (not_135_out, S0);
  and and_57 (and_57_out, not_61_out, S3);
  not not_136 (not_136_out, S2);
  and and_58 (and_58_out, not_62_out, S3);
  not not_137 (not_137_out, S1);
  not not_138 (not_138_out, S0);
  and and_59 (and_59_out, not_63_out, S3);
  not not_139 (not_139_out, S0);
  and and_60 (and_60_out, S4, not_64_out);
  and and_61 (and_61_out, and_9_out, not_65_out);
  and and_62 (and_62_out, and_10_out, LW);
  and and_63 (and_63_out, and_11_out, not_66_out);
  and and_64 (and_64_out, and_12_out, BEQ);
  and and_65 (and_65_out, not_67_out, not_68_out);
  not not_140 (not_140_out, S2);
  and and_66 (and_66_out, S1, S0);
  and and_67 (and_67_out, and_13_out, S2);
  and and_68 (and_68_out, not_69_out, not_70_out);
  and and_69 (and_69_out, and_14_out, S2);
  and and_70 (and_70_out, not_71_out, S0);
  and and_71 (and_71_out, not_72_out, not_73_out);
  not not_141 (not_141_out, S0);
  and and_72 (and_72_out, and_15_out, not_74_out);
  and and_73 (and_73_out, S1, S0);
  and and_74 (and_74_out, and_16_out, S2);
  and and_75 (and_75_out, not_75_out, not_76_out);
  and and_76 (and_76_out, not_77_out, S3);
  not not_142 (not_142_out, S0);
  and and_77 (and_77_out, and_17_out, not_78_out);
  and and_78 (and_78_out, S1, S0);
  and and_79 (and_79_out, and_18_out, S2);
  and and_80 (and_80_out, not_79_out, not_80_out);
  and and_81 (and_81_out, S4, not_81_out);
  not not_143 (not_143_out, S0);
  and and_82 (and_82_out, and_19_out, not_82_out);
  and and_83 (and_83_out, not_83_out, S0);
  and and_84 (and_84_out, and_20_out, not_84_out);
  and and_85 (and_85_out, S1, not_85_out);
  and and_86 (and_86_out, not_86_out, not_87_out);
  not not_144 (not_144_out, S2);
  and and_87 (and_87_out, S1, S0);
  and and_88 (and_88_out, and_21_out, not_88_out);
  and and_89 (and_89_out, and_22_out, SLT);
  and and_90 (and_90_out, and_23_out, not_89_out);
  and and_91 (and_91_out, and_24_out, ADDI);
  and and_92 (and_92_out, not_90_out, not_91_out);
  not not_145 (not_145_out, S1);
  and and_93 (and_93_out, and_25_out, S2);
  and and_94 (and_94_out, S1, not_92_out);
  and and_95 (and_95_out, and_26_out, not_93_out);
  and and_96 (and_96_out, not_94_out, S0);
  and and_97 (and_97_out, not_95_out, S3);
  not not_146 (not_146_out, S2);
  not not_147 (not_147_out, S0);
  and and_98 (and_98_out, and_27_out, S2);
  and and_99 (and_99_out, S1, not_96_out);
  and and_100 (and_100_out, and_28_out, not_97_out);
  and and_101 (and_101_out, not_98_out, S0);
  and and_102 (and_102_out, S4, not_99_out);
  not not_148 (not_148_out, S0);
  and and_103 (and_103_out, and_29_out, not_100_out);
  and and_104 (and_104_out, not_101_out, not_102_out);
  and and_105 (and_105_out, and_30_out, not_103_out);
  and and_106 (and_106_out, S1, not_104_out);
  and and_107 (and_107_out, not_105_out, not_106_out);
  not not_149 (not_149_out, S2);
  and and_108 (and_108_out, S1, S0);
  and and_109 (and_109_out, and_31_out, not_107_out);
  and and_110 (and_110_out, and_32_out, SLT);
  and and_111 (and_111_out, and_33_out, S2);
  and and_112 (and_112_out, not_108_out, not_109_out);
  and and_113 (and_113_out, not_110_out, not_111_out);
  not not_150 (not_150_out, S0);
  and and_114 (and_114_out, and_34_out, not_112_out);
  and and_115 (and_115_out, S1, not_113_out);
  and and_116 (and_116_out, and_35_out, S2);
  and and_117 (and_117_out, not_114_out, not_115_out);
  and and_118 (and_118_out, not_116_out, S3);
  not not_151 (not_151_out, S0);
  and and_119 (and_119_out, and_36_out, not_117_out);
  and and_120 (and_120_out, not_118_out, not_119_out);
  and and_121 (and_121_out, and_37_out, S2);
  and and_122 (and_122_out, not_120_out, not_121_out);
  and and_123 (and_123_out, S4, not_122_out);
  not not_152 (not_152_out, S0);
  and and_124 (and_124_out, and_38_out, and_39_out);
  and and_125 (and_125_out, and_40_out, and_41_out);
  and and_126 (and_126_out, and_42_out, S2);
  and and_127 (and_127_out, and_43_out, EQUAL);
  and and_128 (and_128_out, and_44_out, not_123_out);
  and and_129 (and_129_out, not_124_out, not_125_out);
  and and_130 (and_130_out, and_45_out, not_126_out);
  and and_131 (and_131_out, not_127_out, S0);
  and and_132 (and_132_out, and_46_out, not_128_out);
  and and_133 (and_133_out, S1, S0);
  and and_134 (and_134_out, and_47_out, S2);
  and and_135 (and_135_out, not_129_out, not_130_out);
  and and_136 (and_136_out, and_48_out, S2);
  and and_137 (and_137_out, S1, not_131_out);
  and and_138 (and_138_out, and_49_out, S2);
  and and_139 (and_139_out, S1, S0);
  and and_140 (and_140_out, and_50_out, and_51_out);
  and and_141 (and_141_out, and_52_out, and_53_out);
  and and_142 (and_142_out, and_54_out, S2);
  and and_143 (and_143_out, S1, S0);
  and and_144 (and_144_out, and_55_out, not_132_out);
  and and_145 (and_145_out, not_133_out, S0);
  and and_146 (and_146_out, and_56_out, not_134_out);
  and and_147 (and_147_out, S1, not_135_out);
  and and_148 (and_148_out, and_57_out, not_136_out);
  and and_149 (and_149_out, S1, S0);
  and and_150 (and_150_out, and_58_out, S2);
  and and_151 (and_151_out, not_137_out, not_138_out);
  and and_152 (and_152_out, and_59_out, S2);
  and and_153 (and_153_out, S1, not_139_out);
  and and_154 (and_154_out, and_60_out, S2);
  and and_155 (and_155_out, S1, S0);
  and and_156 (and_156_out, and_61_out, and_62_out);
  and and_157 (and_157_out, and_63_out, and_64_out);
  and and_158 (and_158_out, and_65_out, not_140_out);
  and and_159 (and_159_out, and_66_out, ADDI);
  and and_160 (and_160_out, and_67_out, and_68_out);
  and and_161 (and_161_out, and_69_out, and_70_out);
  and and_162 (and_162_out, and_71_out, S2);
  and and_163 (and_163_out, S1, not_141_out);
  and and_164 (and_164_out, and_72_out, and_73_out);
  and and_165 (and_165_out, and_74_out, and_75_out);
  and and_166 (and_166_out, and_76_out, S2);
  and and_167 (and_167_out, S1, not_142_out);
  and and_168 (and_168_out, and_77_out, and_78_out);
  and and_169 (and_169_out, and_79_out, and_80_out);
  and and_170 (and_170_out, and_81_out, S2);
  and and_171 (and_171_out, S1, not_143_out);
  and and_172 (and_172_out, and_82_out, and_83_out);
  and and_173 (and_173_out, and_84_out, and_85_out);
  and and_174 (and_174_out, and_86_out, not_144_out);
  and and_175 (and_175_out, and_87_out, BEQ);
  and and_176 (and_176_out, and_88_out, and_89_out);
  and and_177 (and_177_out, and_90_out, and_91_out);
  and and_178 (and_178_out, and_92_out, S2);
  and and_179 (and_179_out, not_145_out, S0);
  and and_180 (and_180_out, and_93_out, and_94_out);
  and and_181 (and_181_out, and_95_out, and_96_out);
  and and_182 (and_182_out, and_97_out, not_146_out);
  and and_183 (and_183_out, S1, not_147_out);
  and and_184 (and_184_out, and_98_out, and_99_out);
  and and_185 (and_185_out, and_100_out, and_101_out);
  and and_186 (and_186_out, and_102_out, S2);
  and and_187 (and_187_out, S1, not_148_out);
  and and_188 (and_188_out, and_103_out, and_104_out);
  and and_189 (and_189_out, and_105_out, and_106_out);
  and and_190 (and_190_out, and_107_out, not_149_out);
  and and_191 (and_191_out, and_108_out, SW);
  and and_192 (and_192_out, and_109_out, and_110_out);
  and and_193 (and_193_out, and_111_out, and_112_out);
  and and_194 (and_194_out, and_113_out, S2);
  and and_195 (and_195_out, S1, not_150_out);
  and and_196 (and_196_out, and_114_out, and_115_out);
  and and_197 (and_197_out, and_116_out, and_117_out);
  and and_198 (and_198_out, and_118_out, S2);
  and and_199 (and_199_out, S1, not_151_out);
  and and_200 (and_200_out, and_119_out, and_120_out);
  and and_201 (and_201_out, and_121_out, and_122_out);
  and and_202 (and_202_out, and_123_out, S2);
  and and_203 (and_203_out, S1, not_152_out);
  or or_1 (or_1_out, and_124_out, and_125_out);
  and and_204 (and_204_out, and_126_out, and_127_out);
  and and_205 (and_205_out, and_128_out, and_129_out);
  and and_206 (and_206_out, and_130_out, and_131_out);
  and and_207 (and_207_out, and_132_out, and_133_out);
  and and_208 (and_208_out, and_134_out, and_135_out);
  and and_209 (and_209_out, and_136_out, and_137_out);
  and and_210 (and_210_out, and_138_out, and_139_out);
  or or_2 (or_2_out, and_140_out, and_141_out);
  and and_211 (and_211_out, and_142_out, and_143_out);
  and and_212 (and_212_out, and_144_out, and_145_out);
  and and_213 (and_213_out, and_146_out, and_147_out);
  and and_214 (and_214_out, and_148_out, and_149_out);
  and and_215 (and_215_out, and_150_out, and_151_out);
  and and_216 (and_216_out, and_152_out, and_153_out);
  and and_217 (and_217_out, and_154_out, and_155_out);
  or or_3 (or_3_out, and_156_out, and_157_out);
  and and_218 (and_218_out, and_158_out, and_159_out);
  or or_4 (or_4_out, and_160_out, and_161_out);
  and and_219 (and_219_out, and_162_out, and_163_out);
  or or_5 (or_5_out, and_164_out, and_165_out);
  and and_220 (and_220_out, and_166_out, and_167_out);
  or or_6 (or_6_out, and_168_out, and_169_out);
  and and_221 (and_221_out, and_170_out, and_171_out);
  or or_7 (or_7_out, and_172_out, and_173_out);
  and and_222 (and_222_out, and_174_out, and_175_out);
  or or_8 (or_8_out, and_176_out, and_177_out);
  and and_223 (and_223_out, and_178_out, and_179_out);
  or or_9 (or_9_out, and_180_out, and_181_out);
  and and_224 (and_224_out, and_182_out, and_183_out);
  or or_10 (or_10_out, and_184_out, and_185_out);
  and and_225 (and_225_out, and_186_out, and_187_out);
  or or_11 (or_11_out, and_188_out, and_189_out);
  and and_226 (and_226_out, and_190_out, and_191_out);
  or or_12 (or_12_out, and_192_out, and_193_out);
  and and_227 (and_227_out, and_194_out, and_195_out);
  or or_13 (or_13_out, and_196_out, and_197_out);
  and and_228 (and_228_out, and_198_out, and_199_out);
  or or_14 (or_14_out, and_200_out, and_201_out);
  and and_229 (and_229_out, and_202_out, and_203_out);
  or or_15 (or_15_out, or_1_out, and_204_out);
  or or_16 (or_16_out, and_205_out, and_206_out);
  or or_17 (or_17_out, and_207_out, and_208_out);
  or or_18 (or_18_out, and_209_out, and_210_out);
  or or_19 (or_19_out, or_2_out, and_211_out);
  or or_20 (or_20_out, and_212_out, and_213_out);
  or or_21 (or_21_out, and_214_out, and_215_out);
  or or_22 (or_22_out, and_216_out, and_217_out);
  or or_23 (or_23_out, or_3_out, and_218_out);
  or or_24 (or_24_out, or_4_out, and_219_out);
  or or_25 (or_25_out, or_5_out, and_220_out);
  or or_26 (or_26_out, or_6_out, and_221_out);
  or or_27 (or_27_out, or_7_out, and_222_out);
  or or_28 (or_28_out, or_8_out, and_223_out);
  or or_29 (or_29_out, or_9_out, and_224_out);
  or or_30 (or_30_out, or_10_out, and_225_out);
  or or_31 (or_31_out, or_11_out, and_226_out);
  or or_32 (or_32_out, or_12_out, and_227_out);
  or or_33 (or_33_out, or_13_out, and_228_out);
  or or_34 (or_34_out, or_14_out, and_229_out);
  or or_35 (or_35_out, or_15_out, or_16_out);
  or or_36 (N4, or_35_out, or_37_out);
  or or_37 (or_37_out, or_17_out, or_18_out);
  or or_38 (or_38_out, or_19_out, or_20_out);
  or or_39 (N3, or_38_out, or_40_out);
  or or_40 (or_40_out, or_21_out, or_22_out);
  or or_41 (or_41_out, or_23_out, or_24_out);
  or or_42 (N2, or_41_out, or_43_out);
  or or_43 (or_43_out, or_25_out, or_26_out);
  or or_44 (or_44_out, or_27_out, or_28_out);
  or or_45 (N1, or_44_out, or_46_out);
  or or_46 (or_46_out, or_29_out, or_30_out);
  or or_47 (or_47_out, or_31_out, or_32_out);
  or or_48 (N0, or_47_out, or_49_out);
  or or_49 (or_49_out, or_33_out, or_34_out);
endmodule

module \单总线CPU_中断_微程序  (
  input  [1:0] EduInt,
  output [21:0] \EDU控制总线 ,
  output [4:0] \EDU中断信号 
);

  wire _1_out, _2_out, and_1_out, CLK, comparator_1_eq, comparator_2_eq, equal, mips_alu_1_equal, not_1_out,
       \中断控制器_1_ir1w , \中断控制器_1_ir2w , \中断请求 ;
  wire [4:0] registerfile_1_p4, registerfile_1_p5, \微地址_状态 ;
  wire [11:0] Clks, \指令数 ;
  wire [31:0] AR_q, bit_extender_1_out, controlled_buffer_1_out, controlled_buffer_3_out, DR_q, IR,
       mips_alu_1_result, PC_q, ram_1_data, registerfile_1_p6, shifter_1_out, X_q, Z_q, \内部总线 ;

  // Probe on Clks
  Register #(.width(32), .trigger("rising"), .Select("low")) AR (
    .D(\内部总线 ), .en(\EDU控制总线 [13]), .Q(AR_q), .clk(CLK));  // open: clr
  // Probe on controlled_buffer_3_out
  // Mips_Probe mips_probe_1: pin names not known; wires that end beside it: IR
  Register #(.width(32), .trigger("rising"), .Select("low")) X (
    .D(\内部总线 ), .en(\EDU控制总线 [10]), .Q(X_q), .clk(CLK));  // open: clr
  // Probe on \指令数 
  RAM #(.addrWidth(10), .dataWidth(32), .bus("separate"), .Select("high")) ram_1 (
    .addr(AR_q[11:2]), .din(controlled_buffer_3_out), .data(ram_1_data), .str(\EDU控制总线 [0]), .clk(CLK),
    .ld(\EDU控制总线 [1]));  // open: sel, clr
  MIPS_ALU mips_alu_1 (
    .X(X_q), .Y(\内部总线 ), .Equal(mips_alu_1_equal), .Result(mips_alu_1_result), .ADD(\EDU控制总线 [4]),
    .ADD4(\EDU控制总线 [3]), .SLT(\EDU控制总线 [2]));  // open: SUB
  assign controlled_buffer_1_out = \EDU控制总线 [11] ? \内部总线  : 32'bz;  // Controlled_Buffer controlled_buffer_1
  assign controlled_buffer_1_out = \EDU控制总线 [12] ? ram_1_data : 32'bz;  // Controlled_Buffer controlled_buffer_2
  assign controlled_buffer_3_out = \EDU控制总线 [15] ? DR_q : 32'bz;  // Controlled_Buffer controlled_buffer_3
  // Probe on \内部总线 
  Register #(.width(32), .trigger("rising"), .Select("low")) PC (
    .D(\内部总线 ), .en(\EDU控制总线 [14]), .Q(PC_q), .clk(CLK));  // open: clr
  Register #(.width(32), .trigger("rising"), .Select("low")) DR (
    .D(controlled_buffer_1_out), .Q(DR_q), .clk(CLK));  // open: en, clr
  Register #(.width(1), .trigger("rising"), .Select("low")) PSW (
    .D(mips_alu_1_equal), .en(\EDU控制总线 [7]), .Q(equal), .clk(CLK));  // open: clr
  Register #(.width(32), .trigger("rising"), .Select("low")) Z (
    .D(mips_alu_1_result), .Q(Z_q), .clk(CLK));  // open: en, clr
  assign \内部总线  = \EDU控制总线 [21] ? PC_q : 32'bz;  // Controlled_Buffer controlled_buffer_4
  // Probe on \内部总线 
  assign \内部总线  = \EDU控制总线 [20] ? DR_q : 32'bz;  // Controlled_Buffer controlled_buffer_5
  assign \内部总线  = \EDU控制总线 [19] ? Z_q : 32'bz;  // Controlled_Buffer controlled_buffer_6
  assign \内部总线  = \EDU控制总线 [17] ? bit_extender_1_out : 32'bz;  // Controlled_Buffer controlled_buffer_7
  assign \内部总线  = \EDU控制总线 [16] ? shifter_1_out : 32'bz;  // Controlled_Buffer controlled_buffer_8
  Register #(.width(32), .trigger("rising"), .Select("low")) u_IR (
    .D(\内部总线 ), .en(\EDU控制总线 [8]), .Q(IR), .clk(CLK));  // open: clr
  Comparator #(.width(32), .mode("twosComplement")) comparator_1 (
    .a(IR), .b(32'h1000ffff), .eq(comparator_1_eq));  // open: gt, lt
  Clock #(.highDuration(1), .lowDuration(1)) clock_1 (.out(CLK));
  \微程序控制器_中断  \u_微程序控制器_中断_1  (
    .EQUAL(equal), .\指令字 (IR), .IntR(\中断请求 ), .CLK(CLK), .mAddr(\微地址_状态 ), .ControlBus(\EDU控制总线 ),
    .IntSignals(\EDU中断信号 ));
  // Probe on \微地址_状态 
  // RegisterFile registerfile_1: pin names not known; wires that end beside it: \内部总线 , CLK, \EDU控制总线 [9], registerfile_1_p4, registerfile_1_p5, registerfile_1_p6
  not not_1 (not_1_out, comparator_1_eq);
  Counter #(.width(12), .max('hfff), .ongoal("wrap"), .trigger("rising"), .behavior("new")) counter_1 (
    .count(not_1_out), .Q(Clks), .clk(CLK));  // open: load, D, carry, clr, preset, down
  assign bit_extender_1_out = {{16{IR[15]}}, IR[15:0]};  // Bit_Extender bit_extender_1
  assign \内部总线  = \EDU控制总线 [18] ? registerfile_1_p6 : 32'bz;  // Controlled_Buffer controlled_buffer_9
  Multiplexer #(.select(1), .width(5), .disabled("Z"), .enable("false")) multiplexer_1 (
    .in0(IR[25:21]), .in1(IR[20:16]), .out(registerfile_1_p5), .sel(\EDU控制总线 [6]));
  Multiplexer #(.select(1), .width(5), .disabled("Z"), .enable("false")) multiplexer_2 (
    .in0(IR[20:16]), .in1(IR[15:11]), .out(registerfile_1_p4), .sel(\EDU控制总线 [5]));
  and and_1 (and_1_out, not_1_out, comparator_2_eq);
  Comparator #(.width(5), .mode("twosComplement")) comparator_2 (
    .a(5'b00011), .b(\微地址_状态 ), .eq(comparator_2_eq));  // open: gt, lt
  Shifter #(.width(32), .shift("ll")) shifter_1 (.in(bit_extender_1_out), .\dist (5'b00010), .out(shifter_1_out));
  Counter #(.width(12), .max('hfff), .ongoal("wrap"), .trigger("rising"), .behavior("old")) counter_2 (
    .count(and_1_out), .Q(\指令数 ), .clk(CLK));  // open: load, D, carry, clr, preset
  D_Flip_Flop #(.trigger("rising"), .Pre_Clr_Positions("LEGACY"), .NegatePresetClear("false"), .enable("true"), .NewFFLayout("false")) d_ff_1 (
    .preset(\EDU中断信号 [0]), .reset(\EDU中断信号 [1]));  // open: clk, D, Q, Qn, en
  Button _1 (.out(_1_out));
  Button _2 (.out(_2_out));
  Register #(.width(32), .trigger("rising"), .Select("low")) EPC (.clk(CLK));  // open: D, en, Q, clr
  LED #(.active("true")) _1_2 (.in(\中断控制器_1_ir1w ));
  LED #(.active("true")) _2_2 (.in(\中断控制器_1_ir2w ));
  \中断控制器  \u_中断控制器_1  (
    .CLK(CLK), .Key1(_1_out), .Key2(_2_out), .Clr(\EDU中断信号 [1]), .IR1W(\中断控制器_1_ir1w ),
    .IR2W(\中断控制器_1_ir2w ), .EDU_TEST(EduInt));  // open: IR3W, IntNo, IntR, Key3

  // Other names for the same wires on the sheet: rd[4:0] = IR[15:11]; rt[4:0] = IR[20:16]; rs[4:0] = IR[25:21];
  //   中断控制信号[4:0] = \EDU中断信号 ; 关中断 = \EDU中断信号 [0]; 开中断 = \EDU中断信号 [1]; Addrout = \EDU中断信号 [2]; EPCin = \EDU中断信号 [3];
  //   EPCout = \EDU中断信号 [4]; Write = \EDU控制总线 [0]; 控制总线[21:0] = \EDU控制总线 ; READ = \EDU控制总线 [1]; Slt = \EDU控制总线 [2];
  //   Add4 = \EDU控制总线 [3]; Add = \EDU控制总线 [4]; RegDst = \EDU控制总线 [5]; RegTgt = \EDU控制总线 [6]; PSWin = \EDU控制总线 [7];
  //   IRin = \EDU控制总线 [8]; Rin = \EDU控制总线 [9]; Xin = \EDU控制总线 [10]; DRin = \EDU控制总线 [11]; DREin = \EDU控制总线 [12];
  //   ARin = \EDU控制总线 [13]; PCin = \EDU控制总线 [14]; DREout = \EDU控制总线 [15]; IR_A_out = \EDU控制总线 [16];
  //   IR_I_out = \EDU控制总线 [17]; Rout = \EDU控制总线 [18]; Zout = \EDU控制总线 [19]; DRout = \EDU控制总线 [20];
  //   PCout = \EDU控制总线 [21]

  // Notes on the sheet:
  //   单总线结构 MIPS CPU
  //   MEM
  //   外部总线
  //   内部总线
  //   Immediate32
  //   AddressOffset32
  //   中断使能寄存器
  //   EPC用于保存断点
  //   执行ERET时开中断，同时清除中断源
  //   中断逻辑
endmodule

// 微程序
module \微程序控制器_中断  (
  input  EQUAL,
  input  [31:0] \指令字 ,
  input  IntR,
  input  CLK,
  output [4:0] mAddr,
  output [21:0] ControlBus,
  output [4:0] IntSignals
);

  wire ADDI, BEQ, ERET, LW, P0, P1, P2, SLT, SW;
  wire [4:0] adder_1_out, multiplexer_1_out, undriven, undriven_2, undriven_3, undriven_4,
       \微程序入口查找逻辑_中断_1_s0 ;

  \微程序入口查找逻辑_中断  \u_微程序入口查找逻辑_中断_1  (
    .LW(LW), .SW(SW), .BEQ(BEQ), .SLT(SLT), .ADDI(ADDI), .ERET(ERET), .S4(\微程序入口查找逻辑_中断_1_s0 [4]),
    .S3(\微程序入口查找逻辑_中断_1_s0 [3]), .S2(\微程序入口查找逻辑_中断_1_s0 [2]), .S1(\微程序入口查找逻辑_中断_1_s0 [1]),
    .S0(\微程序入口查找逻辑_中断_1_s0 [0]));
  // Probe on \微程序入口查找逻辑_中断_1_s0 
  \条件判别测试逻辑_中断  \u_条件判别测试逻辑_中断_1  (.P0(P0), .P1(P1), .P2(P2), .equal(EQUAL), .IntR(IntR));  // open: S2, S1, S0
  Multiplexer #(.select(3), .width(5), .disabled("Z"), .enable("false")) multiplexer_1 (
    .in0(undriven_3), .in1(undriven_4), .in2(undriven_2), .in3(undriven), .in4({5{1'b0}}),
    .out(multiplexer_1_out));  // open: in5, in6, in7, sel
  // Probe on multiplexer_1_out
  Register #(.width(5), .trigger("falling"), .Select("low")) register_1 (
    .D(multiplexer_1_out), .Q(mAddr), .clk(CLK));  // open: en, clr
  Adder #(.width(5)) adder_1 (.a(5'b00001), .b(mAddr), .out(adder_1_out));  // open: cin, cout
  \指令译码器  \u_指令译码器_1  (.IR(\指令字 ), .LW(LW), .SW(SW), .BEQ(BEQ), .ADDI(ADDI), .SLT(SLT), .OtherInstr(ERET));
  ROM #(.addrWidth(5), .dataWidth(30), .Select("high")) rom_1 (
    .addr(mAddr), .data({ControlBus, IntSignals, P0, P1, P2}));

  // Notes on the sheet:
  //   不要改变此引脚区域内容，也不要改变封装形式
  //   微程序入口查找逻辑
  //   beq分支
  //   中断响应入口
  //   入口地址
  //   取指微程序入口
  //   顺序地址
  //   判别测试逻辑
  //   μAR
  //   支持中断的微程序控制器（计数器法）
  //   微地址
  //   指令译码器
  //   mAddr++
  //   控制存储器
  //   指令译码信号
  //   控制字段
  //   微指令
  //   指令译码逻辑ID
  //   判断逻辑
endmodule

module \微程序入口查找逻辑_中断  (
  input  LW,
  input  SW,
  input  BEQ,
  input  SLT,
  input  ADDI,
  input  ERET,
  output S4,
  output S3,
  output S2,
  output S1,
  output S0
);
endmodule

module \条件判别测试逻辑_中断  (
  input  P0,
  input  P1,
  input  P2,
  input  equal,
  input  IntR,
  output S2,
  output S1,
  output S0
);
endmodule

// 硬布线
module \硬布线控制器_中断  (
  input  EQUAL,
  input  [31:0] \指令字 ,
  input  IntR,
  input  CLK,
  output [4:0] statu,
  output [21:0] ControlBus,
  output [4:0] IntSignals
);

  wire ADDI, BEQ, ERET, LW, P1, P2, P3, SLT, SW;
  wire [4:0] undriven;

  \硬布线状态机_中断  \u_硬布线状态机_中断_1  ();  // open: S4, S3, S2, S1, S0, LW, SW, BEQ, SLT, ADDI, ERET, IR, EQUAL, N4, N3, N2, N1, N0
  // Probe on undriven
  Register #(.width(5), .trigger("falling"), .Select("low")) register_1 (
    .D(undriven), .Q(statu), .clk(CLK));  // open: en, clr
  // Probe on statu
  \指令译码器  \u_指令译码器_1  (.IR(\指令字 ), .LW(LW), .SW(SW), .BEQ(BEQ), .ADDI(ADDI), .SLT(SLT), .OtherInstr(ERET));
  ROM #(.addrWidth(5), .dataWidth(30), .Select("high")) rom_1 (
    .addr(statu), .data({ControlBus, IntSignals, P1, P2, P3}));

  // Notes on the sheet:
  //   不要改变此引脚区域内容，也不要改变封装形式
  //   硬布线控制器状态机
  //   状态寄存器
  //   支持中断的硬布线控制器
  //   指令译码器
  //   控制存储器
  //   指令译码信号
  //   控制字段
  //   微指令
  //   指令译码逻辑ID
  //   判断逻辑
endmodule

module \硬布线状态机_中断  (
  input  S4,
  input  S3,
  input  S2,
  input  S1,
  input  S0,
  input  LW,
  input  SW,
  input  BEQ,
  input  SLT,
  input  ADDI,
  input  ERET,
  input  IR,
  input  EQUAL,
  output N4,
  output N3,
  output N2,
  output N1,
  output N0
);
endmodule

// ALU
module MIPS_ALU (
  input  ADD,
  input  ADD4,
  input  [31:0] X,
  input  [31:0] Y,
  input  SUB,
  input  SLT,
  output Equal,
  output [31:0] Result
);

  wire [0:0] comparator_1_lt;
  wire [1:0] priority_encoder_1_out;
  wire [31:0] adder_1_out, adder_2_out, subtractor_1_out;

  Pull_Resistor #(.pull(0)) pull_resistor_1 (.node(Y));
  Adder #(.width(32)) adder_1 (.a(X), .b(Y), .out(adder_1_out));  // open: cin, cout
  Adder #(.width(32)) adder_2 (.a(X), .b(32'h4), .out(adder_2_out));  // open: cin, cout
  Subtractor #(.width(32)) subtractor_1 (.a(X), .b(Y), .out(subtractor_1_out));  // open: bin, bout
  Comparator #(.width(32), .mode("twosComplement")) comparator_1 (
    .a(X), .b(Y), .eq(Equal), .lt(comparator_1_lt[0]));  // open: gt
  Priority_Encoder #(.select(2), .disabled("Z")) priority_encoder_1 (
    .in0(ADD), .in1(ADD4), .in2(SUB), .in3(SLT), .out(priority_encoder_1_out));  // open: gs, en_out, en_in
  Pull_Resistor #(.pull(0)) pull_resistor_2 (.node(priority_encoder_1_out));
  Multiplexer #(.select(2), .width(32), .disabled("Z"), .enable("false")) multiplexer_1 (
    .in0(adder_1_out), .in1(adder_2_out), .in2(subtractor_1_out), .in3({{31{1'b0}}, comparator_1_lt[0]}),
    .out(Result), .sel(priority_encoder_1_out));

  // Notes on the sheet:
  //   不要改变此引脚区域内容，也不要改变ALU封装形式
  //   输入引脚
  //   输出引脚
endmodule

// 中断控制器
module \中断控制器  (
  input  CLK,
  input  Key1,
  input  Key2,
  input  Key3,
  input  Clr,
  input  [1:0] EDU_TEST,
  output IR1W,
  output IR2W,
  output IR3W,
  output [1:0] IntNo,
  output IntR
);

  wire and_1_out, and_2_out, and_3_out, Clr0, Clr1, Clr2, Clr3, d_ff_1_q, d_ff_2_q, d_ff_3_q, IR1_q, IR2_q,
       IR3_q, or_1_out, or_3_out, or_6_out, or_7_out, or_8_out;

  or or_1 (or_1_out, Key1, EDU_TEST[0]);
  or or_2 (IR1W, IR1_q, d_ff_2_q);
  or or_3 (or_3_out, Key2, EDU_TEST[1]);
  or or_4 (IR2W, IR2_q, d_ff_3_q);
  D_Flip_Flop #(.trigger("rising"), .Pre_Clr_Positions("LEGACY"), .NegatePresetClear("false"), .enable("true"), .NewFFLayout("false")) d_ff_1 (
    .clk(Key3), .D(1'b1), .Q(d_ff_1_q), .reset(IR3_q));  // open: Qn, preset, en
  or or_5 (IR3W, IR3_q, d_ff_1_q);
  D_Flip_Flop #(.trigger("rising"), .Pre_Clr_Positions("LEGACY"), .NegatePresetClear("false"), .enable("true"), .NewFFLayout("false")) d_ff_2 (
    .clk(or_1_out), .D(1'b1), .Q(d_ff_2_q), .reset(IR1_q));  // open: Qn, preset, en
  D_Flip_Flop #(.trigger("rising"), .Pre_Clr_Positions("LEGACY"), .NegatePresetClear("false"), .enable("true"), .NewFFLayout("false")) d_ff_3 (
    .clk(or_3_out), .D(1'b1), .Q(d_ff_3_q), .reset(IR2_q));  // open: Qn, preset, en
  or or_6 (or_6_out, d_ff_2_q, IR1_q);
  and and_1 (and_1_out, or_6_out, ~Clr1);  // AND_Gate
  or or_7 (or_7_out, d_ff_3_q, IR2_q);
  and and_2 (and_2_out, or_7_out, ~Clr2);  // AND_Gate
  or or_8 (or_8_out, d_ff_1_q, IR3_q);
  and and_3 (and_3_out, or_8_out, ~Clr3);  // AND_Gate
  Pull_Resistor #(.pull(0)) pull_resistor_1 (.node(EDU_TEST));
  D_Flip_Flop #(.trigger("rising"), .Pre_Clr_Positions("LEGACY"), .NegatePresetClear("false"), .enable("true"), .NewFFLayout("false")) IR1 (
    .clk(CLK), .D(and_1_out), .Q(IR1_q));  // open: Qn, preset, en, reset
  D_Flip_Flop #(.trigger("rising"), .Pre_Clr_Positions("LEGACY"), .NegatePresetClear("false"), .enable("true"), .NewFFLayout("false")) IR2 (
    .clk(CLK), .D(and_2_out), .Q(IR2_q));  // open: Qn, preset, en, reset
  D_Flip_Flop #(.trigger("rising"), .Pre_Clr_Positions("LEGACY"), .NegatePresetClear("false"), .enable("true"), .NewFFLayout("false")) IR3 (
    .clk(CLK), .D(and_3_out), .Q(IR3_q));  // open: Qn, preset, en, reset
  Priority_Encoder #(.select(2), .disabled("Z")) priority_encoder_1 (
    .in1(IR1_q), .in2(IR2_q), .in3(IR3_q), .out(IntNo), .gs(IntR));  // open: in0, en_out, en_in
  Decoder #(.select(2), .tristate("false"), .disabled(0), .enable("true")) decoder_1 (
    .out0(Clr0), .out1(Clr1), .out2(Clr2), .out3(Clr3), .sel(IntNo), .en(Clr));

  // Other names for the same wires on the sheet: EDU_INT1 = EDU_TEST[0]; EDU_INT2 = EDU_TEST[1]

  // Notes on the sheet:
  //   中断等待
  //   中断等待
  //   中断等待
  //   中断信号采样参考电路
  //   Reset 
  //   Reset 
  //   Reset 
  //   中断优先编码器
endmodule
